# Fritzing sketch pi-led-light-sensor-diagram (saved by Fritzing 0.9.3b)

parts:
  Raspberry_Pi_1 = Raspberry Pi 3 [part_number=RPI-3-V1.2]
  LED1 = LED - 5mm [color="Red (633nm)" package="5 mm [THT]"]
  R1 = Photocell (LDR) [package=THT]
  R2 = Resistor [tolerance=±5% resistance=220 package=THT]

nets:
  N1: Raspberry_Pi_1.GPIO20, Raspberry_Pi_1.GPIO16, R1.pin_1
  N2: Raspberry_Pi_1.GND, R1.pin_0, R2.Pin_1
  N3: Raspberry_Pi_1.GPIO18, LED1.cathode

notes:
  Photo cell connected at GPIO16
  LED connected at GPIO18
